// Logisim project TermprojectFinalLast2.circ as structural Verilog: 5 circuits, main circuit Core
module Core (
  input  EnS,
  input  [4:0] Move_Address,
  input  Enable_Core,
  input  [7:0] Move_Data_In,
  input  Clk,
  input  [7:0] Fetch_data,
  input  in_7,
  output [7:0] Move_Data_Out,
  output [7:0] Address
);

  wire alu_1_bon, alu_1_boz, and_4_out, control_1_acc_to_mem, control_1_dm_ld, control_1_dm_sel,
       control_1_isbranchn, control_1_isbranchz, control_1_s_alu, control_1_s_alu2, multiplexer_6_out,
       not_1_out, not_2_out, or_1_out;
  wire [1:0] and_2_out, and_3_out, bit_extender_1_out, control_1_acc_data_sel2;
  wire [4:0] multiplexer_3_out;
  wire [7:0] ACC_q, adder_1_out, alu_1_out_8, bit_extender_2_out, controlled_buffer_3_out, multiplexer_1_out,
       multiplexer_2_out, multiplexer_4_out, ram_1_data;

  Multiplexer #(.width(8), .enable("false")) multiplexer_1 (
    .in0({8{1'b0}}), .in1(8'h1), .out(multiplexer_1_out), .sel(EnS));
  assign bit_extender_1_out = {{1{Enable_Core}}, Enable_Core};  // Bit_Extender bit_extender_1
  and and_1 (and_3_out[1], control_1_isbranchn, alu_1_bon);
  Multiplexer #(.select(2), .width(8), .enable("false")) multiplexer_2 (
    .in0(multiplexer_1_out), .in1(bit_extender_2_out), .in2(bit_extender_2_out), .out(multiplexer_2_out),
    .sel(and_2_out));  // open: in3
  assign and_2_out = bit_extender_1_out & and_3_out;  // AND_Gate and_2, 2 bits wide
  and and_3 (and_3_out[0], alu_1_boz, control_1_isbranchz);
  Adder adder_1 (.a(Address), .b(multiplexer_2_out), .out(adder_1_out));  // open: cin, cout
  Register PC (.D(adder_1_out), .Q(Address), .clk(Clk));  // open: en, clr
  Control control_1 (
    .OP0(Fetch_data[7]), .S_Alu(control_1_s_alu), .OP1(Fetch_data[6]), .S_ALu2(control_1_s_alu2),
    .ACC_to_Mem(control_1_acc_to_mem), .OP2(Fetch_data[5]), .ACC_Data_sel(control_1_acc_data_sel2[1]),
    .ACC_Data_Sel2(control_1_acc_data_sel2[0]), .DM_sel(control_1_dm_sel), .isBranchZ(control_1_isbranchz),
    .isBranchN(control_1_isbranchn), .Enb(Enable_Core), .RW(in_7), .DM_Ld(control_1_dm_ld));
  Multiplexer #(.width(5), .enable("false")) multiplexer_3 (
    .in0(Move_Address), .in1(Fetch_data[4:0]), .out(multiplexer_3_out), .sel(Enable_Core));
  assign bit_extender_2_out = {{3{Fetch_data[4]}}, Fetch_data[4:0]};  // Bit_Extender bit_extender_2
  RAM #(.addrWidth(5)) ram_1 (
    .addr(multiplexer_3_out), .data(ram_1_data), .sel(control_1_dm_sel), .clk(Clk), .ld(control_1_dm_ld));  // open: clr
  Multiplexer #(.select(2), .width(8), .enable("false")) multiplexer_4 (
    .in0(controlled_buffer_3_out), .in1(bit_extender_2_out), .in2(alu_1_out_8), .out(multiplexer_4_out),
    .sel(control_1_acc_data_sel2));  // open: in3
  assign Move_Data_Out = or_1_out ? ram_1_data : 8'bz;  // Controlled_Buffer controlled_buffer_1
  assign ram_1_data = multiplexer_6_out ? controlled_buffer_3_out : 8'bz;  // Controlled_Buffer controlled_buffer_2
  assign controlled_buffer_3_out = and_4_out ? ram_1_data : 8'bz;  // Controlled_Buffer controlled_buffer_3
  Multiplexer #(.width(8), .enable("false")) multiplexer_5 (
    .in0(ACC_q), .out(controlled_buffer_3_out), .sel(control_1_acc_to_mem));  // open: in1
  Register ACC (.D(multiplexer_4_out), .en(Enable_Core), .Q(ACC_q), .clk(Clk));  // open: clr
  assign ram_1_data = not_2_out ? Move_Data_In : 8'bz;  // Controlled_Buffer controlled_buffer_4
  Multiplexer #(.enable("false")) multiplexer_6 (
    .in0(and_4_out), .in1(not_1_out), .out(multiplexer_6_out), .sel(Enable_Core));
  not not_1 (not_1_out, and_4_out);
  not not_2 (not_2_out, or_1_out);
  and and_4 (and_4_out, control_1_dm_ld, Enable_Core);
  ALU alu_1 (
    .A(ACC_q), .B(controlled_buffer_3_out), .out_8(alu_1_out_8), .sa1(control_1_s_alu),
    .sa2(control_1_s_alu2), .BOZ(alu_1_boz), .BON(alu_1_bon), .RotateInput(bit_extender_2_out));
  or or_1 (or_1_out, in_7, Enable_Core);

  // Notes on the sheet:
  //   OP
  //   DM
endmodule

module ALU (
  input  [7:0] A,
  input  [7:0] B,
  input  sa1,
  input  sa2,
  input  [7:0] RotateInput,
  output BOZ,
  output BON,
  output [7:0] out_8
);

  wire [7:0] adder_1_out, shifter_1_out, subtractor_1_out;

  Adder adder_1 (.a(A), .b(B), .out(adder_1_out));  // open: cin, cout
  Subtractor subtractor_1 (.a(A), .b(B), .out(subtractor_1_out));  // open: bin, bout
  Comparator comparator_1 (.a(A), .b({8{1'b0}}), .eq(BOZ), .lt(BON));  // open: gt
  Multiplexer #(.select(2), .width(8), .enable("false")) multiplexer_1 (
    .in0(adder_1_out), .in1(subtractor_1_out), .in2(shifter_1_out), .in3(shifter_1_out), .out(out_8),
    .sel({sa1, sa2}));
  Shifter #(.shift("rl")) shifter_1 (.in(A), .\dist (RotateInput[2:0]), .out(shifter_1_out));
endmodule

module Dual_Core (
);

  wire Clock_out, cmu_1_e1, cmu_1_e2, cmu_1_enable, cmu_1_rw1, cmu_1_rw2;
  wire [4:0] cmu_1_move1_address, cmu_1_move2_address;
  wire [7:0] cmu_1_c1_data, cmu_1_c2_data, cmu_1_r1_address, cmu_1_r2_address, core_1_address,
       core_1_move_data_out, core_2_address, core_2_move_data_out;
  wire [10:0] rom_1_data, rom_2_data;

  Core core_1 (
    .Address(core_1_address), .Fetch_data(cmu_1_c1_data), .Move_Data_Out(core_1_move_data_out),
    .Enable_Core(cmu_1_enable), .Move_Address(cmu_1_move1_address), .Clk(Clock_out), .in_7(cmu_1_rw1),
    .Move_Data_In(core_2_move_data_out), .EnS(cmu_1_e2));
  Core core_2 (
    .Address(core_2_address), .Fetch_data(cmu_1_c2_data), .Move_Data_Out(core_2_move_data_out),
    .Enable_Core(cmu_1_enable), .Move_Address(cmu_1_move2_address), .Clk(Clock_out), .in_7(cmu_1_rw2),
    .Move_Data_In(core_1_move_data_out), .EnS(cmu_1_e1));
  Clock Clock (.out(Clock_out));
  CMU cmu_1 (
    .C1_Address(core_1_address), .C1_Data(cmu_1_c1_data), .C2_Address(core_2_address),
    .C2_Data(cmu_1_c2_data), .R1_Address(cmu_1_r1_address), .R1_Data(rom_1_data),
    .R2_Address(cmu_1_r2_address), .R2_Data(rom_2_data), .RW1(cmu_1_rw1), .RW2(cmu_1_rw2),
    .Move1_Address(cmu_1_move1_address), .Move2_Address(cmu_1_move2_address), .Enable(cmu_1_enable),
    .E1(cmu_1_e1), .E2(cmu_1_e2));
  ROM #(.dataWidth(11)) rom_1 (.addr(cmu_1_r1_address), .data(rom_1_data));  // open: sel
  ROM #(.dataWidth(11)) rom_2 (.addr(cmu_1_r2_address), .data(rom_2_data));  // open: sel

  // Notes on the sheet:
  //   contents of rom_1 (hex, n*v repeats v):
  //   82 40 83 41 81 42 83 43 a1 61 c1 c0 44 80
  //   contents of rom_2 (hex, n*v repeats v):
  //   84 40 85 41 81 42 83 43 a1 61 c1 c0 44 485 80
endmodule

module CMU (
  input  [7:0] C1_Address,
  input  [10:0] R1_Data,
  input  [7:0] C2_Address,
  input  [10:0] R2_Data,
  output E1,
  output Enable,
  output [4:0] Move1_Address,
  output RW1,
  output [7:0] R1_Address,
  output [7:0] C1_Data,
  output [7:0] R2_Address,
  output [7:0] C2_Data,
  output RW2,
  output [4:0] Move2_Address,
  output E2
);

  not not_1 (E1, R1_Data[10]);
  not not_2 (E2, R2_Data[10]);
  nor nor_1 (Enable, R2_Data[10], R1_Data[10]);
  Multiplexer #(.select(2), .width(5), .enable("false")) multiplexer_1 (
    .in1(R1_Data[9:5]), .in2(R2_Data[4:0]), .out(Move1_Address), .sel({R2_Data[10], R1_Data[10]}));  // open: in0, in3
  Multiplexer #(.select(2), .width(5), .enable("false")) multiplexer_2 (
    .in1(R1_Data[4:0]), .in2(R2_Data[9:5]), .out(Move2_Address), .sel({R2_Data[10], R1_Data[10]}));  // open: in0, in3

  assign C1_Data = R1_Data[7:0];
  assign C2_Data = R2_Data[7:0];
  assign R1_Address = C1_Address;
  assign R2_Address = C2_Address;
  assign RW1 = R1_Data[10];
  assign RW2 = R2_Data[10];
endmodule

module Control (
  input  OP0,
  input  OP1,
  input  OP2,
  input  Enb,
  input  RW,
  output S_Alu,
  output S_ALu2,
  output ACC_to_Mem,
  output ACC_Data_sel,
  output ACC_Data_Sel2,
  output DM_sel,
  output DM_Ld,
  output isBranchN,
  output isBranchZ
);

  wire and_1_out, and_2_out, and_3_out, and_4_out, and_6_out, and_7_out, not_2_out, not_3_out, not_4_out,
       not_5_out, not_6_out, not_7_out, not_8_out, or_2_out, or_3_out, or_5_out;

  not not_1 (S_Alu, OP0);
  and and_1 (and_1_out, OP1, OP2);
  and and_2 (and_2_out, OP0, OP1);
  not not_2 (not_2_out, OP1);
  not not_3 (not_3_out, OP2);
  not not_4 (not_4_out, OP2);
  and and_3 (and_3_out, OP0, OP2);
  and and_4 (and_4_out, OP0, OP1);
  or or_1 (ACC_Data_sel, and_1_out, and_2_out);
  and and_5 (ACC_Data_Sel2, OP0, not_2_out, not_3_out);
  and and_6 (and_6_out, OP1, not_4_out);
  and and_7 (and_7_out, OP0, OP2);
  or or_2 (or_2_out, and_3_out, and_4_out);
  not not_5 (not_5_out, OP0);
  not not_6 (not_6_out, OP1);
  not not_7 (not_7_out, OP2);
  or or_3 (or_3_out, and_6_out, and_7_out);
  and and_8 (isBranchN, not_5_out, not_6_out, OP2);
  and and_9 (isBranchZ, not_6_out, not_5_out, not_7_out);
  not not_8 (not_8_out, Enb);
  or or_4 (ACC_to_Mem, OP0, RW);
  or or_5 (or_5_out, or_2_out, not_8_out);
  or or_6 (DM_sel, or_3_out, not_8_out);
  Multiplexer #(.enable("false")) multiplexer_1 (.in0(RW), .in1(or_5_out), .out(DM_Ld), .sel(Enb));

  assign S_ALu2 = OP2;
endmodule
