// Logisim project Termproject2.circ as structural Verilog: 5 circuits, main circuit Core
module Core (
  input  Enable_Core,
  input  [7:0] Move_Data,
  input  [7:0] Fetch_data,
  output [7:0] Move_Address,
  output [7:0] Address
);

  wire clock_1_out, control_1_acc_to_mem, control_1_dm_ld, control_1_dm_sel, control_1_s_alu;
  wire [1:0] control_1_acc_data_sel2;
  wire [7:0] ACC_q, adder_1_out, alu_1_out_4, bit_extender_1_out, multiplexer_1_out, ram_1_data;

  Adder adder_1 (.a(Address), .b(8'h1), .out(adder_1_out));  // open: cin, cout
  Register PC (.D(adder_1_out), .Q(Address), .clk(clock_1_out));  // open: en, clr
  Control control_1 (
    .OP(Fetch_data[2]), .OP1(Fetch_data[1]), .OP2(Fetch_data[0]), .S_ALU(control_1_s_alu),
    .ACC_to_Mem(control_1_acc_to_mem), .ACC_Data_Sel(control_1_acc_data_sel2[1]),
    .ACC_Data_Sel2(control_1_acc_data_sel2[0]), .DM_Sel(control_1_dm_sel), .DM_Ld(control_1_dm_ld));
  Clock clock_1 (.out(clock_1_out));
  assign bit_extender_1_out = {{3{Fetch_data[7]}}, Fetch_data[7:3]};  // Bit_Extender bit_extender_1
  Multiplexer #(.select(2), .width(8), .enable("false")) multiplexer_1 (
    .in0(ram_1_data), .in1(bit_extender_1_out), .in2(alu_1_out_4), .out(multiplexer_1_out),
    .sel(control_1_acc_data_sel2));  // open: in3
  RAM #(.addrWidth(5)) ram_1 (
    .addr(Fetch_data[7:3]), .data(ram_1_data), .sel(control_1_dm_sel), .clk(clock_1_out), .ld(control_1_dm_ld));  // open: clr
  Multiplexer #(.width(8), .enable("false")) multiplexer_2 (
    .in0(ACC_q), .out(ram_1_data), .sel(control_1_acc_to_mem));  // open: in1
  Register ACC (.D(multiplexer_1_out), .Q(ACC_q), .clk(clock_1_out));  // open: en, clr
  ALU alu_1 (.A(ACC_q), .B(ram_1_data), .out_4(alu_1_out_4), .S_ALU(control_1_s_alu));

  // Notes on the sheet:
  //   OP
  //   DM
endmodule

module ALU (
  input  [7:0] A,
  input  [7:0] B,
  input  S_ALU,
  output [7:0] out_4
);

  wire [7:0] adder_1_out, subtractor_1_out;

  Adder adder_1 (.a(A), .b(B), .out(adder_1_out));  // open: cin, cout
  Subtractor subtractor_1 (.a(A), .b(B), .out(subtractor_1_out));  // open: bin, bout
  Multiplexer #(.width(8), .enable("false")) multiplexer_1 (
    .in0(adder_1_out), .in1(subtractor_1_out), .out(out_4), .sel(S_ALU));
endmodule

module Control (
  input  OP,
  input  OP1,
  input  OP2,
  output S_ALU,
  output ACC_to_Mem,
  output ACC_Data_Sel,
  output ACC_Data_Sel2,
  output DM_Sel,
  output DM_Ld
);

  wire not_2_out, not_3_out;

  not not_1 (ACC_to_Mem, OP);
  and and_1 (ACC_Data_Sel, OP, OP1);
  not not_2 (not_2_out, OP1);
  not not_3 (not_3_out, OP2);
  or or_1 (DM_Sel, OP2, OP1);
  not not_4 (DM_Ld, OP);
  and and_2 (ACC_Data_Sel2, not_2_out, not_3_out);

  assign S_ALU = OP2;
endmodule

module Dual_Core (
);

  wire cmu_1_core1_enable, cmu_1_core2_enable;
  wire [7:0] cmu_1_c1_data, cmu_1_c2_data, cmu_1_r1_address, cmu_1_r2_address, core_1_address,
       core_1_move_address, core_2_address, core_2_move_address, undriven;
  wire [10:0] rom_1_data, rom_2_data;

  Core core_1 (
    .Address(core_1_address), .Fetch_data(cmu_1_c1_data), .Move_Data(undriven),
    .Enable_Core(cmu_1_core1_enable), .Move_Address(core_1_move_address));
  Core core_2 (
    .Address(core_2_address), .Fetch_data(cmu_1_c2_data), .Move_Data(undriven),
    .Enable_Core(cmu_1_core2_enable), .Move_Address(core_2_move_address));
  CMU cmu_1 (
    .C1_Address(core_1_address), .C1_Data(cmu_1_c1_data), .C2_Address(core_2_address),
    .C2_Data(cmu_1_c2_data), .R1_Address(cmu_1_r1_address), .R1_Data(rom_1_data),
    .R2_Address(cmu_1_r2_address), .R2_Data(rom_2_data), .Core2_Enable(cmu_1_core2_enable),
    .Core1_Enable(cmu_1_core1_enable), .Move2_Address(core_2_move_address),
    .Move1_Address(core_1_move_address));
  ROM #(.dataWidth(11)) rom_1 (.addr(cmu_1_r1_address), .data(rom_1_data));  // open: sel
  ROM #(.dataWidth(11)) rom_2 (.addr(cmu_1_r2_address), .data(rom_2_data));  // open: sel
endmodule

module CMU (
  input  [7:0] C1_Address,
  input  [10:0] R1_Data,
  input  [7:0] C2_Address,
  input  [10:0] R2_Data,
  output Core1_Enable,
  output [7:0] Move1_Address,
  output [7:0] R1_Address,
  output [7:0] C1_Data,
  output [7:0] R2_Address,
  output [7:0] C2_Data,
  output Core2_Enable,
  output [7:0] Move2_Address
);

  Multiplexer #(.width(8), .enable("false")) multiplexer_1 (
    .in0(R1_Data[7:0]), .out(C1_Data), .sel(R1_Data[10]));  // open: in1

  assign R1_Address = C1_Address;
endmodule
