// Logisim project TermprojectT3.circ as structural Verilog: 6 circuits, main circuit Core
module Core (
  input  [4:0] Move_Address,
  input  Enable_Core,
  input  [7:0] Move_Data_In,
  input  [7:0] Fetch_data,
  output [7:0] Move_Data_Out,
  output [7:0] Address
);

  wire alu_1_bon, alu_1_boz, clock_1_out, control2_1_acc_to_mem, control2_1_dm_ld, control2_1_dm_sel,
       control2_1_isbranchn, control2_1_isbranchz, control2_1_s_alu, control2_1_s_alu2;
  wire [1:0] and_2_out, control2_1_acc_data_sel2;
  wire [4:0] multiplexer_2_out;
  wire [7:0] ACC_q, adder_1_out, alu_1_out_7, bit_extender_1_out, multiplexer_1_out, multiplexer_3_out,
       ram_1_data;

  and and_1 (and_2_out[1], control2_1_isbranchn, alu_1_bon);
  Multiplexer #(.select(2), .width(8), .enable("false")) multiplexer_1 (
    .in0(8'h1), .in1(bit_extender_1_out), .in2(bit_extender_1_out), .out(multiplexer_1_out), .sel(and_2_out));  // open: in3
  and and_2 (and_2_out[0], alu_1_boz, control2_1_isbranchz);
  Adder adder_1 (.a(Address), .b(multiplexer_1_out), .out(adder_1_out));  // open: cin, cout
  Register PC (.D(adder_1_out), .Q(Address), .clk(clock_1_out));  // open: en, clr
  Control2 control2_1 (
    .OP0(Fetch_data[2]), .S_Alu(control2_1_s_alu), .OP1(Fetch_data[1]), .S_ALu2(control2_1_s_alu2),
    .ACC_to_Mem(control2_1_acc_to_mem), .OP2(Fetch_data[0]), .ACC_Data_sel(control2_1_acc_data_sel2[1]),
    .ACC_Data_Sel2(control2_1_acc_data_sel2[0]), .DM_sel(control2_1_dm_sel), .DM_Ld(control2_1_dm_ld),
    .isBranchZ(control2_1_isbranchz), .isBranchN(control2_1_isbranchn));
  Multiplexer #(.width(5), .enable("false")) multiplexer_2 (
    .in0(Move_Address), .in1(Fetch_data[7:3]), .out(multiplexer_2_out), .sel(Enable_Core));
  Clock clock_1 (.out(clock_1_out));
  assign bit_extender_1_out = {{3{Fetch_data[7]}}, Fetch_data[7:3]};  // Bit_Extender bit_extender_1
  Multiplexer #(.select(2), .width(8), .enable("false")) multiplexer_3 (
    .in0(ram_1_data), .in1(bit_extender_1_out), .in2(alu_1_out_7), .out(multiplexer_3_out),
    .sel(control2_1_acc_data_sel2));  // open: in3
  RAM #(.addrWidth(5)) ram_1 (
    .addr(multiplexer_2_out), .data(ram_1_data), .sel(control2_1_dm_sel), .clk(clock_1_out),
    .ld(control2_1_dm_ld));  // open: clr
  Multiplexer #(.width(8), .enable("false")) multiplexer_4 (
    .in0(ACC_q), .out(ram_1_data), .sel(control2_1_acc_to_mem));  // open: in1
  Register ACC (.D(multiplexer_3_out), .Q(ACC_q), .clk(clock_1_out));  // open: en, clr
  ALU alu_1 (
    .A(ACC_q), .B(ram_1_data), .out_7(alu_1_out_7), .sa1(control2_1_s_alu), .sa2(control2_1_s_alu2),
    .BOZ(alu_1_boz), .BON(alu_1_bon));

  // Notes on the sheet:
  //   OP
  //   DM
endmodule

module ALU (
  input  [7:0] A,
  input  [7:0] B,
  input  sa1,
  input  sa2,
  output BOZ,
  output BON,
  output [7:0] out_7
);

  wire [7:0] adder_1_out, shifter_1_out, subtractor_1_out;

  Adder adder_1 (.a(A), .b(B), .out(adder_1_out));  // open: cin, cout
  Subtractor subtractor_1 (.a(A), .b(B), .out(subtractor_1_out));  // open: bin, bout
  Comparator comparator_1 (.a(A), .b({8{1'b0}}), .eq(BOZ), .lt(BON));  // open: gt
  Multiplexer #(.select(2), .width(8), .enable("false")) multiplexer_1 (
    .in0(adder_1_out), .in1(subtractor_1_out), .in2(shifter_1_out), .in3(shifter_1_out), .out(out_7),
    .sel({sa1, sa2}));
  Shifter #(.shift("rl")) shifter_1 (.in(A), .\dist (A[2:0]), .out(shifter_1_out));
endmodule

module Control (
  input  OP,
  input  OP1,
  input  OP2,
  output S_ALU,
  output ACC_to_Mem,
  output ACC_Data_Sel,
  output ACC_Data_Sel2,
  output DM_Sel,
  output DM_Ld
);

  wire not_2_out, not_3_out;

  not not_1 (ACC_to_Mem, OP);
  and and_1 (ACC_Data_Sel, OP, OP1);
  not not_2 (not_2_out, OP1);
  not not_3 (not_3_out, OP2);
  or or_1 (DM_Sel, OP2, OP1);
  not not_4 (DM_Ld, OP);
  and and_2 (ACC_Data_Sel2, not_2_out, not_3_out);

  assign S_ALU = OP2;
endmodule

module Dual_Core (
);

  wire cmu_1_core1_enable, cmu_1_core2_enable;
  wire [4:0] cmu_1_move1_address, cmu_1_move2_address;
  wire [7:0] cmu_1_c1_data, cmu_1_c2_data, cmu_1_r1_address, cmu_1_r2_address, core_1_address,
       core_1_move_data_out, core_2_address, core_2_move_data_out;
  wire [10:0] rom_1_data, rom_2_data;

  Core core_1 (
    .Address(core_1_address), .Fetch_data(cmu_1_c1_data), .Move_Data_Out(core_1_move_data_out),
    .Enable_Core(cmu_1_core1_enable), .Move_Address(cmu_1_move1_address), .Move_Data_In(core_2_move_data_out));
  Core core_2 (
    .Address(core_2_address), .Fetch_data(cmu_1_c2_data), .Move_Data_Out(core_2_move_data_out),
    .Enable_Core(cmu_1_core2_enable), .Move_Address(cmu_1_move2_address), .Move_Data_In(core_1_move_data_out));
  CMU cmu_1 (
    .C1_Address(core_1_address), .C1_Data(cmu_1_c1_data), .C2_Address(core_2_address),
    .C2_Data(cmu_1_c2_data), .R1_Address(cmu_1_r1_address), .R1_Data(rom_1_data),
    .R2_Address(cmu_1_r2_address), .R2_Data(rom_2_data), .Core2_Enable(cmu_1_core2_enable),
    .Core1_Enable(cmu_1_core1_enable), .Move2_Address(cmu_1_move2_address),
    .Move1_Address(cmu_1_move1_address));
  ROM #(.dataWidth(11)) rom_1 (.addr(cmu_1_r1_address), .data(rom_1_data));  // open: sel
  ROM #(.dataWidth(11)) rom_2 (.addr(cmu_1_r2_address), .data(rom_2_data));  // open: sel

  // Notes on the sheet:
  //   contents of rom_1 (hex, n*v repeats v):
  //   b
endmodule

module CMU (
  input  [7:0] C1_Address,
  input  [10:0] R1_Data,
  input  [7:0] C2_Address,
  input  [10:0] R2_Data,
  output Core1_Enable,
  output [4:0] Move1_Address,
  output [7:0] R1_Address,
  output [7:0] C1_Data,
  output [7:0] R2_Address,
  output [7:0] C2_Data,
  output Core2_Enable,
  output [4:0] Move2_Address
);

  not not_1 (Core1_Enable, R1_Data[10]);
  not not_2 (Core2_Enable, R1_Data[10]);

  assign C1_Data = R1_Data[7:0];
  assign Move1_Address = R1_Data[9:5];
  assign Move2_Address = R1_Data[4:0];
  assign R1_Address = C1_Address;
endmodule

module Control2 (
  input  OP0,
  input  OP1,
  input  OP2,
  output S_Alu,
  output S_ALu2,
  output ACC_to_Mem,
  output ACC_Data_sel,
  output ACC_Data_Sel2,
  output DM_sel,
  output DM_Ld,
  output isBranchN,
  output isBranchZ
);

  wire and_1_out, and_2_out, and_3_out, and_4_out, and_6_out, and_7_out, not_2_out, not_3_out, not_4_out,
       not_5_out, not_6_out, not_7_out;

  not not_1 (S_Alu, OP0);
  and and_1 (and_1_out, OP1, OP2);
  and and_2 (and_2_out, OP0, OP1);
  not not_2 (not_2_out, OP1);
  not not_3 (not_3_out, OP2);
  not not_4 (not_4_out, OP2);
  and and_3 (and_3_out, OP0, OP2);
  and and_4 (and_4_out, OP0, OP1);
  or or_1 (ACC_Data_sel, and_1_out, and_2_out);
  and and_5 (ACC_Data_Sel2, OP0, not_2_out, not_3_out);
  and and_6 (and_6_out, OP1, not_4_out);
  and and_7 (and_7_out, OP0, OP2);
  or or_2 (DM_Ld, and_3_out, and_4_out);
  not not_5 (not_5_out, OP0);
  not not_6 (not_6_out, OP1);
  not not_7 (not_7_out, OP2);
  or or_3 (DM_sel, and_6_out, and_7_out);
  and and_8 (isBranchN, not_5_out, not_6_out, OP2);
  and and_9 (isBranchZ, not_6_out, not_5_out, not_7_out);

  assign ACC_to_Mem = OP0;
  assign S_ALu2 = OP2;
endmodule
