// Logisim project TermprojectT4.circ as structural Verilog: 5 circuits, main circuit Core
module Core (
  input  [4:0] Move_Address,
  input  Enable_Core,
  input  Clk,
  input  [7:0] Fetch_data,
  output [7:0] Move_Data_Out,
  output [7:0] Address
);

  wire alu_1_bon, alu_1_boz, control_1_p4, control_1_p5, control_1_p6, control_1_p9, control_1_p10,
       control_1_p11, control_1_p12;
  wire [1:0] and_2_out, control_1_p8;
  wire [4:0] multiplexer_2_out;
  wire [7:0] ACC_q, adder_1_out, alu_1_out_7, bit_extender_1_out, multiplexer_1_out, multiplexer_3_out;

  and and_1 (and_2_out[1], control_1_p11, alu_1_bon);
  Multiplexer #(.select(2), .width(8), .enable("false")) multiplexer_1 (
    .in0(8'h1), .in1(bit_extender_1_out), .in2(bit_extender_1_out), .out(multiplexer_1_out), .sel(and_2_out));  // open: in3
  and and_2 (and_2_out[0], alu_1_boz, control_1_p12);
  Adder adder_1 (.a(Address), .b(multiplexer_1_out), .out(adder_1_out));  // open: cin, cout
  Register PC (.D(adder_1_out), .Q(Address), .clk(Clk));  // open: en, clr
  // Control control_1: pin names not known; wires that end beside it: Fetch_data[2], Fetch_data[1], Fetch_data[0], control_1_p4, control_1_p5, control_1_p6, control_1_p8[1], control_1_p8[0], control_1_p9, control_1_p10, control_1_p11, control_1_p12
  Multiplexer #(.width(5), .enable("false")) multiplexer_2 (
    .in0(Move_Address), .in1(Fetch_data[7:3]), .out(multiplexer_2_out), .sel(Enable_Core));
  assign bit_extender_1_out = {{3{Fetch_data[7]}}, Fetch_data[7:3]};  // Bit_Extender bit_extender_1
  Multiplexer #(.select(2), .width(8), .enable("false")) multiplexer_3 (
    .in0(Move_Data_Out), .in1(bit_extender_1_out), .in2(alu_1_out_7), .out(multiplexer_3_out),
    .sel(control_1_p8));  // open: in3
  RAM #(.addrWidth(5)) ram_1 (
    .addr(multiplexer_2_out), .data(Move_Data_Out), .sel(control_1_p9), .clk(Clk), .ld(control_1_p10));  // open: clr
  Multiplexer #(.width(8), .enable("false")) multiplexer_4 (
    .in0(ACC_q), .out(Move_Data_Out), .sel(control_1_p6));  // open: in1
  Register ACC (.D(multiplexer_3_out), .Q(ACC_q), .clk(Clk));  // open: en, clr
  ALU alu_1 (
    .A(ACC_q), .B(Move_Data_Out), .out_7(alu_1_out_7), .sa1(control_1_p4), .sa2(control_1_p5),
    .BOZ(alu_1_boz), .BON(alu_1_bon));

  // Notes on the sheet:
  //   OP
  //   DM
endmodule

module ALU (
  input  [7:0] A,
  input  [7:0] B,
  input  sa1,
  input  sa2,
  output BOZ,
  output BON,
  output [7:0] out_7
);

  wire [7:0] adder_1_out, shifter_1_out, subtractor_1_out;

  Adder adder_1 (.a(A), .b(B), .out(adder_1_out));  // open: cin, cout
  Subtractor subtractor_1 (.a(A), .b(B), .out(subtractor_1_out));  // open: bin, bout
  Comparator comparator_1 (.a(A), .b({8{1'b0}}), .eq(BOZ), .lt(BON));  // open: gt
  Multiplexer #(.select(2), .width(8), .enable("false")) multiplexer_1 (
    .in0(adder_1_out), .in1(subtractor_1_out), .in2(shifter_1_out), .in3(shifter_1_out), .out(out_7),
    .sel({sa1, sa2}));
  Shifter #(.shift("rl")) shifter_1 (.in(A), .\dist (A[2:0]), .out(shifter_1_out));
endmodule

module Dual_Core (
);

  wire clock_1_out, cmu_1_p5, cmu_1_p6;
  wire [4:0] cmu_1_p7, cmu_1_p8;
  wire [7:0] cmu_1_p2, cmu_1_p4, cmu_1_p9, cmu_1_p11, core_1_address, core_1_move_data_out, core_2_address;
  wire [10:0] cmu_1_p10, cmu_1_p12;

  Core core_1 (
    .Address(core_1_address), .Fetch_data(cmu_1_p2), .Move_Data_Out(core_1_move_data_out),
    .Enable_Core(cmu_1_p5), .Move_Address(cmu_1_p8), .Clk(clock_1_out));
  Core core_2 (
    .Address(core_2_address), .Fetch_data(cmu_1_p4), .Move_Data_Out(core_1_move_data_out),
    .Enable_Core(cmu_1_p6), .Move_Address(cmu_1_p7));  // open: Clk
  Clock clock_1 (.out(clock_1_out));
  // CMU cmu_1: pin names not known; wires that end beside it: core_1_address, cmu_1_p2, core_2_address, cmu_1_p4, cmu_1_p5, cmu_1_p6, cmu_1_p7, cmu_1_p8, cmu_1_p9, cmu_1_p10, cmu_1_p11, cmu_1_p12
  ROM #(.dataWidth(11)) rom_1 (.addr(cmu_1_p9), .data(cmu_1_p10));  // open: sel
  ROM #(.dataWidth(11)) rom_2 (.addr(cmu_1_p11), .data(cmu_1_p12));  // open: sel

  // Notes on the sheet:
  //   contents of rom_1 (hex, n*v repeats v):
  //   a ff 11 22 33 44 ab
endmodule

module CMU (
  input  [7:0] C1_Address,
  input  [10:0] R1_Data,
  input  [7:0] C2_Address,
  input  [10:0] R2_Data,
  output Core1_Enable,
  output [4:0] Move1_Address,
  output RW1,
  output [7:0] R1_Address,
  output [7:0] C1_Data,
  output [7:0] R2_Address,
  output [7:0] C2_Data,
  output RW2,
  output [4:0] Move2_Address
);

  nor nor_1 (Core1_Enable, R2_Data[0], R1_Data[0]);
  Multiplexer #(.select(2), .width(5), .enable("false")) multiplexer_1 (
    .in1(R1_Data[5:1]), .in2(R2_Data[10:6]), .out(Move1_Address), .sel({R2_Data[0], R1_Data[0]}));  // open: in0, in3
  Multiplexer #(.select(2), .width(5), .enable("false")) multiplexer_2 (
    .in1(R1_Data[10:6]), .in2(R2_Data[5:1]), .out(Move2_Address), .sel({R2_Data[0], R1_Data[0]}));  // open: in0, in3

  assign C1_Data = R1_Data[10:3];
  assign C2_Data = R2_Data[10:3];
  assign R1_Address = C1_Address;
  assign RW1 = R1_Data[0];
  assign RW2 = R2_Data[0];
endmodule

module Control (
  input  OP0,
  input  OP1,
  input  OP2,
  input  Enb,
  input  RW,
  output S_Alu,
  output S_ALu2,
  output ACC_to_Mem,
  output ACC_Data_sel,
  output ACC_Data_Sel2,
  output DM_sel,
  output DM_Ld,
  output isBranchN,
  output isBranchZ
);

  wire and_1_out, and_2_out, and_3_out, and_4_out, and_6_out, and_7_out, not_2_out, not_3_out, not_4_out,
       not_5_out, not_6_out, not_7_out, not_8_out, or_2_out, or_3_out, or_5_out;

  not not_1 (S_Alu, OP0);
  and and_1 (and_1_out, OP1, OP2);
  and and_2 (and_2_out, OP0, OP1);
  not not_2 (not_2_out, OP1);
  not not_3 (not_3_out, OP2);
  not not_4 (not_4_out, OP2);
  and and_3 (and_3_out, OP0, OP2);
  and and_4 (and_4_out, OP0, OP1);
  or or_1 (ACC_Data_sel, and_1_out, and_2_out);
  and and_5 (ACC_Data_Sel2, OP0, not_2_out, not_3_out);
  and and_6 (and_6_out, OP1, not_4_out);
  and and_7 (and_7_out, OP0, OP2);
  or or_2 (or_2_out, and_3_out, and_4_out);
  not not_5 (not_5_out, OP0);
  not not_6 (not_6_out, OP1);
  not not_7 (not_7_out, OP2);
  or or_3 (or_3_out, and_6_out, and_7_out);
  not not_8 (not_8_out, Enb);
  and and_8 (isBranchN, not_5_out, not_6_out, OP2);
  and and_9 (isBranchZ, not_6_out, not_5_out, not_7_out);
  or or_4 (DM_sel, or_3_out, not_8_out);
  or or_5 (or_5_out, or_2_out, not_8_out);
  Multiplexer #(.enable("false")) multiplexer_1 (.in0(RW), .in1(or_5_out), .out(DM_Ld), .sel(Enb));

  assign ACC_to_Mem = OP0;
  assign S_ALu2 = OP2;
endmodule
